# Fritzing sketch 595shiftregister33 (saved by Fritzing 0.9.2b)
circuit board: 8.46667cm x 5.64444cm
breadboards: 1

parts:
  U1 = 74HC595 [package="DIP16 [THT]"]
  R1 = Resistor [tolerance=±5% resistance=220 package=THT]
  R2 = Resistor [tolerance=±5% resistance=220 package=THT]
  R3 = Resistor [tolerance=±5% resistance=220 package=THT]
  R4 = Resistor [tolerance=±5% resistance=220 package=THT]
  R5 = Resistor [tolerance=±5% resistance=220 package=THT]
  R6 = Resistor [tolerance=±5% resistance=220 package=THT]
  R7 = Resistor [tolerance=±5% resistance=220 package=THT]
  R8 = Resistor [tolerance=±5% resistance=220 package=THT]
  LED2 = LED - 5mm [color="Red (633nm)" package="5 mm [THT]"]
  LED3 = LED - 5mm [color="Red (633nm)" package="5 mm [THT]"]
  LED4 = LED - 5mm [color="Red (633nm)" package="5 mm [THT]"]
  LED5 = LED - 5mm [color="Red (633nm)" package="5 mm [THT]"]
  LED6 = LED - 5mm [color="Red (633nm)" package="5 mm [THT]"]
  LED7 = LED - 5mm [color="Red (633nm)" package="5 mm [THT]"]
  LED8 = LED - 5mm [color="Red (633nm)" package="5 mm [THT]"]
  LED1 = LED - 3mm [color="Red (633nm)" package="3 mm [THT]"]
  WeMos_D1_Mini1 = WeMos D1 Mini

nets:
  N1: U1.Q1, R7.Pin_0
  N2: U1.Q2, R6.Pin_0
  N3: U1.Q3, R5.Pin_0
  N4: U1.Q4, R4.Pin_0
  N5: U1.Q5, R3.Pin_0
  N6: U1.Q6, R2.Pin_0
  N7: U1.Q7, R1.Pin_0
  GND: U1.GND, U1.OE, LED2.cathode, LED3.cathode, LED4.cathode, LED5.cathode, LED6.cathode, LED7.cathode, LED8.cathode, LED1.cathode
  N8: U1.SH_CP, WeMos_D1_Mini1.D8
  N9: U1.ST_CP, WeMos_D1_Mini1.D7
  N10: U1.DS, WeMos_D1_Mini1.D6
  N11: U1.Q0, R8.Pin_0
  VCC: U1.VCC, WeMos_D1_Mini1.3V3
  N12: R1.Pin_1, LED1.anode
  N13: R2.Pin_1, LED2.anode
  N14: R3.Pin_1, LED3.anode
  N15: R4.Pin_1, LED4.anode
  N16: R5.Pin_1, LED5.anode
  N17: R6.Pin_1, LED6.anode
  N18: R7.Pin_1, LED7.anode
  N19: R8.Pin_1, LED8.anode
