# Fritzing sketch PI AND ADS1015 (saved by Fritzing 0.9.3b)

parts:
  Part1 = Adafruit ADS1015 12Bit I2C ADC [part_number="Adafruit #1083"]
  Raspberry_Pi1 = Raspberry Pi 2

nets:
  N1: Part1.SDA, Raspberry_Pi1.GPIO2
  N2: Part1.SCL, Raspberry_Pi1.GPIO3
  GND: Part1.GND, Raspberry_Pi1.GND
  VDD: Part1.VDD, Raspberry_Pi1.3v3

custom parts:
  Adafruit ADS1015 12Bit I2C ADC: For microcontrollers without an analog-to-digital converter or when you want a higher-precision ADC, the ADS1015 provides 12-bit precision at 3300 samples/second over I2C. The chip can be configured as 4 single-ended input channels, or two differential channels. As a nice bonus, it even includes a programmable gain amplifier, up to x16, to help boost up smaller single/differential signals to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
