# Fritzing sketch wemos ads1015 (saved by Fritzing 0.9.3b)

parts:
  Part1 = Adafruit ADS1015 12Bit I2C ADC [part_number="Adafruit #1083"]
  WeMos_D1_Mini1 = WeMos D1 Mini

nets:
  N1: Part1.SDA, WeMos_D1_Mini1.D2
  N2: Part1.SCL, WeMos_D1_Mini1.D1
  N3: Part1.GND, WeMos_D1_Mini1.G
  VDD: Part1.VDD, WeMos_D1_Mini1.3V3

custom parts:
  Adafruit ADS1015 12Bit I2C ADC: For microcontrollers without an analog-to-digital converter or when you want a higher-precision ADC, the ADS1015 provides 12-bit precision at 3300 samples/second over I2C. The chip can be configured as 4 single-ended input channels, or two differential channels. As a nice bonus, it even includes a programmable gain amplifier, up to x16, to help boost up smaller single/differential signals to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
