# Fritzing sketch wemos and 4067 analog (saved by Fritzing 0.9.3b)

parts:
  WeMos_D1_Mini1 = WeMos D1 Mini
  Part1 = Analog Digital MUX Breakout
  R1 = Resistor [tolerance=±5% resistance=220 package=THT]
  R2 = Resistor [tolerance=±5% resistance=220 package=THT]

nets:
  3V3: WeMos_D1_Mini1.3V3, Part1.VCC
  N1: WeMos_D1_Mini1.A0, Part1.SIG
  N2: WeMos_D1_Mini1.D5, Part1.S0
  N3: WeMos_D1_Mini1.D6, Part1.S1
  N4: WeMos_D1_Mini1.D7, Part1.S2
  N5: WeMos_D1_Mini1.D8, Part1.S3
  N6: WeMos_D1_Mini1.G, Part1.GND
  N7: Part1.C0, R1.Pin_1, R2.Pin_0
  GND: Part1.EN, R2.Pin_1
  3.3V: R1.Pin_0
