# Fritzing sketch wemos and MAG3110 (saved by Fritzing 0.9.3b)

parts:
  Part5 = MAG3110
  WeMos_D1_Mini1 = WeMos D1 Mini

nets:
  N1: Part5.GND, WeMos_D1_Mini1.G
  VCC: Part5.VCC, WeMos_D1_Mini1.3V3
  N2: Part5.SDA, WeMos_D1_Mini1.D2
  N3: Part5.SCL, WeMos_D1_Mini1.D1

custom parts:
  MAG3110: Sparkfun MAG3110 Breakout
