# Fritzing sketch wemos and dust sensor (saved by Fritzing 0.9.3b)

parts:
  R1 = Resistor [tolerance=±5% resistance=220 package=THT]
  C1 = Electrolytic Capacitor [capacitance=0.22mF voltage=16V package="100 mil [THT, electrolytic]"]
  J1 = female pin header, 6 pins [form="♀ (female)"]
  WeMos_D1_Mini1 = WeMos D1 Mini

nets:
  N1: R1.Pin_1, C1.+
  N2: C1.-, J1.pin2, J1.pin4
  N3: J1.pin3, WeMos_D1_Mini1.D2
  N4: J1.pin5, WeMos_D1_Mini1.D0
  N5: J1.pin6, WeMos_D1_Mini1.3V3
  GND: WeMos_D1_Mini1.G
