# Fritzing sketch wemos and hmc5883l (saved by Fritzing 0.9.3b)

parts:
  Part1 = Triple Axis Magnetometer - HMC5883 Breakout
  WeMos_D1_Mini1 = WeMos D1 Mini

nets:
  N1: Part1.GND, WeMos_D1_Mini1.G
  VCC: Part1.VCC, WeMos_D1_Mini1.3V3
  N2: Part1.SDA, WeMos_D1_Mini1.D2
  N3: Part1.SCL, WeMos_D1_Mini1.D1
