# Fritzing sketch wemos and i2c lcd (saved by Fritzing 0.9.3b)

parts:
  U1 = LCD-16X2 [package=lcd-16x2]
  LCM1602_IIC2 = LCM1602 IIC [part_number="LCM1602 IIC" chip_label="LCM1602 IIC" package="DIP (Dual Inline) [THT]"]
  WeMos_D1_Mini1 = WeMos D1 Mini

nets:
  VSS: U1.VSS, LCM1602_IIC2.VSS
  VDD: U1.VDD, LCM1602_IIC2.VDD
  N1: U1.VO, LCM1602_IIC2.V0
  N2: U1.RS, LCM1602_IIC2.RS
  N3: U1.R_W, LCM1602_IIC2.RW
  N4: U1.E, LCM1602_IIC2.E
  N5: U1.DB0, LCM1602_IIC2.D0
  N6: U1.DB1, LCM1602_IIC2.D1
  N7: U1.DB2, LCM1602_IIC2.D2
  N8: U1.DB3, LCM1602_IIC2.D3
  N9: U1.DB4, LCM1602_IIC2.D4
  N10: U1.DB5, LCM1602_IIC2.D5
  N11: U1.DB6, LCM1602_IIC2.D6
  N12: U1.DB7, LCM1602_IIC2.D7
  N13: U1.A, LCM1602_IIC2.A
  N14: U1.K, LCM1602_IIC2.K
  N15: LCM1602_IIC2.GND, WeMos_D1_Mini1.G
  VCC: LCM1602_IIC2.VCC, WeMos_D1_Mini1.3V3
  N16: LCM1602_IIC2.SDA, WeMos_D1_Mini1.D2
  N17: LCM1602_IIC2.SCL, WeMos_D1_Mini1.D1
  N18: LCM1602_IIC2.LED_A, LCM1602_IIC2.LED_B

custom parts:
  LCM1602 IIC: I2C-Module to use a 1602 or 2004 LCD on with the wire.h libory Serial LCD Modul

// code stored in the sketch: hygroThermoLCD.ino
/* How to use the DHT-22 sensor with Arduino uno
   Temperature and humidity sensor
   More info: http://www.ardumotive.com/how-to-use-dht-22-sensor-en.html
   Dev: Michalis Vasilakis // Date: 1/7/2015 // www.ardumotive.com */

//Libraries
#include <DHT.h>
#include <Wire.h> 
#include <LCD.h>
#include <LiquidCrystal_I2C.h>

//Constants
#define DHTPIN 4     // what pin we're connected to
#define DHTTYPE DHT22   // DHT 22  (AM2302)
DHT dht(DHTPIN, DHTTYPE); //// Initialize DHT sensor for normal 16mhz Arduino

//ALWAYS USE THIS WITH LCD I2C and Addres 0x3F
#define I2C_ADDR 0x3F
#define BACKLIGHT_PIN 3
#define En_pin 2
#define Rw_pin 1
#define Rs_pin 0
#define D4_pin 4
#define D5_pin 5
#define D6_pin 6
#define D7_pin 7
LiquidCrystal_I2C lcd(I2C_ADDR,En_pin,Rw_pin,Rs_pin,D4_pin,D5_pin,D6_pin,D7_pin);

//Variables
int chk;
float hum;  //Stores humidity value
float temp; //Stores temperature value

void setup()
{
  Serial.begin(9600);
  dht.begin();
  lcd.begin(16,2);
  lcd.setBacklightPin(BACKLIGHT_PIN,POSITIVE);
  lcd.setBacklight(HIGH);
}

void loop()
{
  
  delay(2000);
  //Read data and store it to variables hum and temp
  hum = dht.readHumidity();
  temp = dht.readTemperature();
  //Print temp and humidity values to serial monitor
  Serial.print("Humidity: ");
  Serial.print(hum);
  Serial.print(" %, Temp: ");
  Serial.print(temp);
  Serial.println(" Celsius");

  lcd.clear();
  lcd.setCursor(0,0);
  lcd.print("Temp: ");
  lcd.print(temp);
  lcd.print(" ");
  lcd.print((char)223);
  lcd.print("C");
  lcd.setCursor(0,1);
  lcd.print("Hum:  ");
  lcd.print(hum);
  lcd.print(" %");

  delay(2000); //Delay 2 sec.

}
