# Fritzing sketch wemos and ir (saved by Fritzing 0.9.3b)

parts:
  WeMos_D1_Mini1 = WeMos D1 Mini
  Grove1 = Grove Infrared Receiver

nets:
  3V3: WeMos_D1_Mini1.3V3, Grove1.VCC
  N1: WeMos_D1_Mini1.D4, Grove1.RX
  N2: WeMos_D1_Mini1.G, Grove1.GND
