# Fritzing sketch wemos and l9110 (saved by Fritzing 0.9.3b)

parts:
  U1 = L9110 H-bridge module [part_number="L9110 H-bridge"]
  M1 = DC Motor
  WeMos_D1_Mini1 = WeMos D1 Mini
  Power_plug1 = Power plug

nets:
  GND: U1.GND, Power_plug1.GND
  VCC: U1.VCC, Power_plug1.VCC
  N1: U1.A-IA, WeMos_D1_Mini1.D3
  N2: U1.A-IB, WeMos_D1_Mini1.D4
  N3: U1.MOTOR_A-A, M1.pin_2
  N4: U1.MOTOR_A-B, M1.pin_1
