# Fritzing sketch wemos and ldr (saved by Fritzing 0.9.3b)

parts:
  R1 = Resistor [tolerance=±5% resistance=10k package=THT]
  WeMos_D1_Mini1 = WeMos D1 Mini
  LDR = Photocell (LDR) [package=THT]

nets:
  N1: R1.Pin_0, WeMos_D1_Mini1.A0, LDR.pin_1
  N2: R1.Pin_1, WeMos_D1_Mini1.G
  N3: WeMos_D1_Mini1.3V3, LDR.pin_0
