# Fritzing sketch wemos and lm35 (saved by Fritzing 0.9.3b)

parts:
  WeMos_D1_Mini1 = WeMos D1 Mini
  T1 = LM35 Temperature Sensor [package="TO92 [THT]"]

nets:
  N1: WeMos_D1_Mini1.3V3, T1.+Vs
  N2: WeMos_D1_Mini1.A0, T1.Vout
  N3: WeMos_D1_Mini1.G, T1.GND
