# Fritzing sketch wemos and lsm303 (saved by Fritzing 0.9.3b)

parts:
  Part1 = Adafruit LSM303DLHC Triple-axis Accelerometer+Magnetometer (Compass) [part_number="Adafruit #1120"]
  WeMos_D1_Mini1 = WeMos D1 Mini

nets:
  N1: Part1.SCL, WeMos_D1_Mini1.D1
  N2: Part1.SDA, WeMos_D1_Mini1.D2
  N3: Part1.GND, WeMos_D1_Mini1.G
  3.3V: Part1.3.3V, WeMos_D1_Mini1.3V3

custom parts:
  Adafruit LSM303DLHC Triple-axis Accelerometer+Magnetometer (Compass): He told you "Go West, young maker!" - but you don't know which way is West! Ah, if only you had this triple-axis accelerometer/magnetometer compass module. Inside are two sensors, one is a classic 3-axis accelerometer, which can tell you which direction is down towards the Earth (by measuring gravity). The other is a magnetometer that can sense where the strongest magnetic force is coming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
