# Fritzing sketch wemos and oled (saved by Fritzing 0.9.3b)

parts:
  Squix1 = OLED 0.96" 128x64 I2C SSD1306
  WeMos_D1_Mini1 = WeMos D1 Mini

nets:
  VCC: Squix1.VCC, WeMos_D1_Mini1.3V3
  N1: Squix1.GND, WeMos_D1_Mini1.G
  N2: Squix1.SCL, WeMos_D1_Mini1.D1
  N3: Squix1.SCA, WeMos_D1_Mini1.D2
