# Fritzing sketch wemos and pcf8574 (saved by Fritzing 0.9.3b)
breadboards: 1

parts:
  U1 = PCF8574 [package="DIP16 [THT]"]
  LED1 = LED - 5mm [color="Red (633nm)" package="5 mm [THT]"]
  LED2 = LED - 5mm [color="Red (633nm)" package="5 mm [THT]"]
  WeMos_D1_Mini1 = WeMos D1 Mini

nets:
  N1: U1.A0, U1.A1, U1.A3, U1.GND, WeMos_D1_Mini1.G
  N2: U1.P0, LED1.anode
  N3: U1.P1, LED2.anode
  N4: U1.SCL, WeMos_D1_Mini1.D1
  N5: U1.SDA, WeMos_D1_Mini1.D2
  VCC: U1.VCC, WeMos_D1_Mini1.3V3
  N6: LED1.cathode, LED2.cathode
