# Fritzing sketch wemos and sht11 (saved by Fritzing 0.9.3b)

parts:
  Part1 = SHT1x-Breakout
  WeMos_D1_Mini1 = WeMos D1 Mini

nets:
  N1: Part1.SCK, WeMos_D1_Mini1.D3
  N2: Part1.DATA, WeMos_D1_Mini1.D4
  VCC: Part1.VCC, WeMos_D1_Mini1.3V3
  N3: Part1.GND, WeMos_D1_Mini1.G
