# Fritzing sketch wemos and sht21 (saved by Fritzing 0.9.3b)

parts:
  Part1 = HTU21D-F Temperature + Humidity Sensor
  WeMos_D1_Mini1 = WeMos D1 Mini

nets:
  +3V3: Part1.+3V3, WeMos_D1_Mini1.3V3
  N1: Part1.GND, WeMos_D1_Mini1.G
  N2: Part1.SDA, WeMos_D1_Mini1.D2
  N3: Part1.SCL, WeMos_D1_Mini1.D1

custom parts:
  HTU21D-F Temperature + Humidity Sensor: This I2C digital humidity sensor is an accurate and intelligent alternative to the much simpler Humidity and Temperature Sensor - SHT15 Breakout It has a typical accuracy of ±2% with an operating range that's optimized from 5% to 95% RH. Operation outside this range is still possible - just the accuracy might drop a bit. The temperature output has an accuracy of ±1°C from -30~90°C. If you're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
