# Fritzing sketch wemos and sht31 (saved by Fritzing 0.9.3b)

parts:
  Part1 = Adafruit SHT31-D Sensirion Temperature/Humidity Sensor [part_number="Adafruit #2857"]
  WeMos_D1_Mini1 = WeMos D1 Mini

nets:
  VIN: Part1.VIN, WeMos_D1_Mini1.3V3
  N1: Part1.GND, WeMos_D1_Mini1.G
  N2: Part1.SCL, WeMos_D1_Mini1.D1
  N3: Part1.SDA, WeMos_D1_Mini1.D2

custom parts:
  Adafruit SHT31-D Sensirion Temperature/Humidity Sensor: Sensirion Temperature/Humidity sensors are some of the finest & highest-accuracy devices you can get. And, finally we have some that have a true I2C interface for easy reading. The SHT31-D sensor has an excellent ±2% relative humidity and ±0.3°C accuracy for most uses. Unlike earlier SHT sensors, this sensor has a true I2C interface, and (bonus!) even with two address options. It also is 3V or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
