# Fritzing sketch wemos mini and ds18b20 (saved by Fritzing 0.9.3b)
breadboards: 1

parts:
  DS1 = DS18B20 1-Wire Temperature Sensor [part_number=DS18B20]
  R1 = Resistor [tolerance=±5% resistance=4.7k package=THT]
  WeMos_D1_Mini1 = WeMos D1 Mini

nets:
  VDD: DS1.VDD, R1.Pin_0, WeMos_D1_Mini1.5V
  N1: DS1.DQ, R1.Pin_1, WeMos_D1_Mini1.D4
  N2: DS1.GND, WeMos_D1_Mini1.G
